# Fritzing sketch fritzing_schematics (saved by Fritzing 0.9.3b)
breadboards: 1

parts:
  Part1 = Arduino Uno (Rev3)
  S1 = Momentary Switch [package=tactile-pth]
  S2 = Momentary Switch [package=tactile-pth]
  S3 = Momentary Switch [package=tactile-pth]
  R1 = Resistor [tolerance=±5% resistance=220 package=THT]
  R2 = Resistor [tolerance=±5% resistance=220 package=THT]
  R3 = Resistor [tolerance=±5% resistance=220 package=THT]
  Power_plug1 = Power plug
  M1 = DC Motor
  S4 = H-Bridge with L298N

nets:
  N1: Part1.D10_PWM/SS, S3.3, R3.Pin_0
  N2: Part1.D11_PWM/MOSI, S2.3, R2.Pin_0
  N3: Part1.D12/MISO, S1.3, R1.Pin_0
  N4: Part1.D3_PWM, S4.ENA
  N5: Part1.D4, S4.IN1
  N6: Part1.D5_PWM, S4.IN2
  N7: Part1.5V, S1.4, S2.4, S3.4
  GND: Part1.GND, R1.Pin_1, R2.Pin_1, R3.Pin_1, Power_plug1.GND, S4.GND
  VCC: Power_plug1.VCC, S4.12V
  N8: M1.pin_1, S4.M1-02
  N9: M1.pin_2, S4.M1-01

notes:
  12 volt power supply

custom parts:
  H-Bridge with L298N: h-bridge
